# Fritzing sketch Smart parking (saved by Fritzing 0.9.3b)
breadboards: 1

parts:
  U1 = NodeMCU V1.0
  Part2 = Arduino Mega 2560 (Rev3)
  LCD1 = LCD screen
  U2 = POT [package=pot_alpha_rv16af-20]
  J2 = Basic Servo
  J3 = Basic Servo
  M1 = fc-51 [package=THT]
  M2 = fc-51 [package=THT]
  hc-sr1 = hc-sr04

nets:
  N1: U1.D0, Part2.D9_PWM
  N2: U1.D1, Part2.D10_PWM
  N3: Part2.A0, M2.pin1
  N4: Part2.A1, M1.pin1
  GND: Part2.GND, LCD1.VSS, LCD1.R/W, LCD1.LED-, U2.E, J2.gnd, J3.gnd, M1.pin2, M2.pin2, hc-sr1.GND
  N5: Part2.D13_PWM, hc-sr1.Trig
  N6: Part2.D12_PWM, hc-sr1.Echo
  N7: Part2.D4_PWM, J3.pulse
  N8: Part2.D5_PWM, J2.pulse
  VCC: Part2.5V, LCD1.VDD, LCD1.LED+, U2.A, J2.vcc, J3.vcc, M1.pin3, M2.pin3, hc-sr1.VCC
  N9: Part2.D31, LCD1.DB7
  N10: Part2.D33, LCD1.DB6
  N11: Part2.D35, LCD1.DB5
  N12: Part2.D37, LCD1.DB4
  N13: Part2.D39, LCD1.E
  N14: Part2.D41, LCD1.RS
  N15: LCD1.V0, U2.S

custom parts:
  NodeMCU V1.0: ESP8266 based NodeMCU
