# Fritzing sketch Smart parking (saved by Fritzing 0.9.3b)
circuit board: 8.46667cm x 5.64444cm
breadboards: 1

parts:
  hc-sr1 = hc-sr04
  U1 = LCD-16X2 [package=lcd-16x2_noholes]
  J1 = Basic Servo
  U3 = NodeMCU V1.0
  U4 = ESP8266 WiFi Module [part_number=ESP8266]  # not connected
  U5 = POT [package=pot_alpha_rv16af-20]
  LED1 = smd LED [color="Red (633nm)" package="0603 [SMD]"]
  RJ-1 = RJ-11 Connector with Breakout Board
  RJ-2 = RJ-11 Connector with Breakout Board
  J2 = Basic Servo

nets:
  VCC: hc-sr1.VCC, U1.VDD, J1.vcc, U3.Vin, U5.E, LED1.anode, RJ-1.Vcc, RJ-2.Vcc, J2.vcc
  N1: hc-sr1.Trig, U3.SD2
  N2: hc-sr1.Echo, U3.SD3
  GND: hc-sr1.GND, U1.VSS, J1.gnd, U3.GND, U5.A, LED1.cathode, RJ-1.GND, RJ-2.GND, J2.gnd
  N3: U1.VO, U5.S
  N4: U1.RS, U3.D4
  N5: U1.E, U3.A0
  N6: U1.DB4, U3.D0
  N7: U1.DB5, U3.D1
  N8: U1.DB6, U3.D2
  N9: U1.DB7, U3.D3
  N10: J1.pulse, U3.D7
  N11: U3.D5, RJ-2.PRB
  N12: U3.D6, RJ-1.PRB
  N13: U3.D8, J2.pulse

custom parts:
  Basic Servo: A generic servo.
  NodeMCU V1.0: ESP8266 based NodeMCU

// code stored in the sketch: Smart Parking.ino
#include <LiquidCrystal.h>

#include <ESP8266WiFi.h>
#include <Servo.h>
// #include <LiquidCrystal_I2C.h>
#include <Wire.h>
#include <FirebaseArduino.h>

#define FIREBASE_HOST "iot-smart-parking-23cf0-default-rtdb.firebaseio.com"                 // the project name address from firebase id
#define FIREBASE_AUTH "o4PAQ1w0Aqtsv82seAwrNrBpwyrDKETVsA9QR4Bb"            // the secret key generated from firebase

#define WIFI_SSID "GEARBOX STAFF"                                             // input your home or public wifi name 
#define WIFI_PASSWORD "Staff@Gearbox"                                    //password for Wifi
String Available = "";                                                  //availability string
String fireAvailable = "";

// LiquidCrystal_I2C lcd(0x27, 16, 2);         //i2c display address 27 and 16x2 lcd display


// initialize the library with the numbers of the interface pins
LiquidCrystal lcd(7, 8, 9, 10, 11, 12);

Servo myservo;                          //servo as gate
Servo myservos;                               //servo as gate
int Empty;                            //available space integer
int allSpace = 90;
int countYes = 0;
int carEnter = D0;                      // entry sensor 
int carExited = D4;                   //exi sensor
int TRIG = D7;                  //ultrasonic trig  pin
int ECHO = D8;                // ultrasonic echo pin
int led = D3;                 // spot occupancy signal
int pos;
int pos1;

long duration, distance;     

void setup() {

  
  delay(1000);
  Serial.begin (9600);     // serial debugging
  Wire.begin(D2, D1);       // i2c start
  myservo.attach(D6);      // servo pin to D6
  myservos.attach(D5);       // servo pin to D5
  pinMode(TRIG, OUTPUT);      // trig pin as output 
  pinMode(ECHO, INPUT);         // echo pin as input
  pinMode(led, OUTPUT);         // spot indication
  pinMode(carExited, INPUT);    // ir as input
  pinMode(carEnter, INPUT);     // ir as input

  WiFi.begin(WIFI_SSID, WIFI_PASSWORD);                                     //try to connect with wifi
  Serial.print("Connecting to ");
  Serial.print(WIFI_SSID);                          // display ssid
  while (WiFi.status() != WL_CONNECTED) {
    Serial.print(".");                          // if not connected print this
    delay(500);
  }
  Serial.println();
  Serial.print("Connected to ");
  Serial.println(WIFI_SSID);
  Serial.print("IP Address is : ");
  Serial.println(WiFi.localIP());                                            //print local IP address
  Firebase.begin(FIREBASE_HOST, FIREBASE_AUTH);        // begin firebase authentication

  //lcd.begin();                           //begin lcd

   // set up the LCD's number of columns and rows:
  lcd.begin(16, 2);
  
  lcd.home();                            
  lcd.setCursor(0, 0);                      // 0th row and 0thh column
  lcd.print("Smart Parking");    
}

void loop() {

  digitalWrite(TRIG, LOW);         // make trig pin low
  delayMicroseconds(2);
  digitalWrite(TRIG, HIGH);        // make trig pin high
  delayMicroseconds(10);
  digitalWrite(TRIG, LOW);
  duration = pulseIn(ECHO, HIGH);
  distance = (duration / 2) / 29.1;      // take distance in cm

    Serial.print("Centimeter: ");
    Serial.println(distance);

  int carEntry = digitalRead(carEnter);      // read ir input
  if (carEntry == HIGH) {                     // if high then count and send data
    countYes++;                             //increment count
    Serial.print("Car Entered = " ); Serial.println(countYes );
    lcd.setCursor(0, 1);
    lcd.print("Car Entered");
    for (pos = 140; pos >= 45; pos -= 1) {        // change servo position
      myservos.write(pos);                       
      delay(5);
    }
    delay(2000);

    for (pos = 45; pos <= 140; pos += 1) {       // change servo position
      // in steps of 1 degree
      myservos.write(pos);
      delay(5);
    }

    Firebase.pushString("/Parking Status/", fireAvailable );    // send string to firebase
    lcd.clear();
  }
  int carExit = digitalRead(carExited);              //read exit ir sensor
  if (carExit == HIGH) {                            //if high then count and send
    countYes--;                                    //decrement count
    Serial.print("Car Exited = " ); Serial.println(countYes);
    lcd.setCursor(0, 1);
    lcd.print("Car Exited");
    for (pos1 = 140; pos1 >= 45; pos1 -= 1) {         // change servo position
      myservo.write(pos1);
      delay(5);
    }
    delay(2000);

    for (pos1 = 45; pos1 <= 140; pos1 += 1) {            // change servo position
      // in steps of 1 degree
      myservo.write(pos1);
      delay(5);
    }
    Firebase.pushString("/Parking Status/", fireAvailable );  // send string to firebase
    lcd.clear();
  }
  if (distance < 6) {                      //if distance is less than 6cm then on led 
        Serial.println("Occupied ");
    digitalWrite(led, HIGH);
  }

  if (distance > 6) {                        //if distance is greater than 6cm then off led 
        Serial.println("Available ");
    digitalWrite(led, LOW);
  }

  Empty = allSpace - countYes;         //calculate available data
 
  Available = String("Available= ") + String(Empty) + String("/") + String(allSpace);       // convert the int to string
  fireAvailable = String("Available=") + String(Empty) + String("/") + String(allSpace);

  lcd.setCursor(0, 0);
  lcd.print(Available);                 //print available data to lcd

}
